# Fritzing sketch rover fritzing (saved by Fritzing 0.9.3b)

parts:
  DC_Mot_Enc1 = DC Motor with two-phase hall-encoder [part_number=VT-E-G25A-06-177E]
  DC_Mot_Enc2 = DC Motor with two-phase hall-encoder [part_number=VT-E-G25A-06-177E]
  DC_Mot_Enc3 = DC Motor with two-phase hall-encoder [part_number=VT-E-G25A-06-177E]
  DC_Mot_Enc4 = DC Motor with two-phase hall-encoder [part_number=VT-E-G25A-06-177E]
  U1 = ESP32S-HiLetgo [part_number=ESP32S-HiLetgo]
  J1 = STM32 Nucleo boards
  J2 = STM32 Nucleo boards
  Componente1 = SRF05 Ultrasonic Rangefinder
  Componente2 = SRF05 Ultrasonic Rangefinder
  Componente3 = SRF05 Ultrasonic Rangefinder
  A1 = Sabertooth2x12
  A2 = Sabertooth2x12
  U2 = LIPO-2000mAh [package=lipo-2000]
  A3 = XY-3606
  KF-1 = KF-301 Relay [package=THT]
  KF-2 = KF-301 Relay [package=THT]

nets:
  N1: DC_Mot_Enc1.pin1, A1.Pin_10
  N2: DC_Mot_Enc1.pin2, A1.Pin_9
  N3: DC_Mot_Enc1.pin3, DC_Mot_Enc2.pin3, A1.Pin_2
  N4: DC_Mot_Enc1.pin4, J2.PC12
  N5: DC_Mot_Enc1.pin5, J2.PB2
  N6: DC_Mot_Enc1.pin6, DC_Mot_Enc2.pin6, J2.GND#1189
  N7: DC_Mot_Enc2.pin1, A1.Pin_6
  N8: DC_Mot_Enc2.pin2, A1.Pin_5
  N9: DC_Mot_Enc2.pin4, J2.PA12
  N10: DC_Mot_Enc2.pin5, J2.PA11
  N11: DC_Mot_Enc3.pin1, A2.Pin_10
  N12: DC_Mot_Enc3.pin2, A2.Pin_9
  N13: DC_Mot_Enc3.pin3, DC_Mot_Enc4.pin3, A2.Pin_2
  N14: DC_Mot_Enc3.pin4, J2.PA4
  N15: DC_Mot_Enc3.pin5, J2.PC6
  N16: DC_Mot_Enc3.pin6, DC_Mot_Enc4.pin6
  N17: DC_Mot_Enc4.pin1, A2.Pin_6
  N18: DC_Mot_Enc4.pin2, A2.Pin_5
  N19: DC_Mot_Enc4.pin4, J2.PA1
  N20: DC_Mot_Enc4.pin5, J2.PA0
  N21: U1.GPIO21, J2.PB7
  N22: U1.GPIO22, J2.PC0
  N23: J1.PC8, Componente1.Trig
  N24: J1.GND#229, KF-1.NO
  N25: J1.PC11, Componente3.Trig
  N26: J1.PD2, KF-1.signal
  N27: J1.E5V, J2.E5V, A3.Pin_4
  5V: J1.5V, Componente3.VCC, KF-2.power
  N28: J1.GND#1189, Componente3.GND, KF-2.ground
  N29: J1.PC9, Componente1.Echo
  N30: J1.PA6, J2.PA6
  N31: J1.PA7, J2.PA7
  N32: J1.PA9, Componente2.Trig
  N33: J1.PA8, Componente2.Echo
  N34: J1.PB4, J2.PB5
  N35: J1.PB5, J2.PB4
  N36: J1.PB3, J2.PA5
  N37: J1.PA10, KF-2.NO
  N38: J1.PC10, Componente3.Echo
  N39: J1.PC12, KF-2.signal
  N40: J2.GND#333, A1.Pin_8, A2.Pin_8, U2.-, A3.Pin_2, A3.Pin_3
  N41: J2.GND#1188, A1.Pin_1, A2.Pin_1
  N42: J2.PC4, KF-1.NC
  N43: J2.PB10, KF-2.NC
  N44: A1.Pin_3, KF-1.C
  N45: A1.Pin_7, A2.Pin_7, U2.+, A3.Pin_1
  N46: A2.Pin_3, KF-2.C

custom parts:
  ESP32S-HiLetgo: HiLetgo ESP-WROOM-32 ESP32 ESP-32S Development Board 2.4GHz Dual-Mode WiFi + Bluetooth Dual Cores Microcontroller The ESP32 integrated with Antenna switches, RF Balun, power amplifiers, low-noise amplifiers, filters, and management modules, and the entire solution occupies the least area of PCB. 2.4 GHz Wi-Fi plus Bluetooth dual-mode chip, with TSMC Ultra-low power consumption 40nm technology,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
  Sabertooth2x12: The Sabertooth 2X12 is one of the most versatile, efficient and easy to use dual motor drivers on the market.
  XY-3606: 24V/12V turn 5V 5A power module, DC-DC XY-3606 Power Converter Super LM2596S.
  KF-301 Relay: KF-301
